// Digital circuit contador.dig as structural Verilog
module contador (
  input  CLK,
  input  in_2
);

  wire D0_nq, or_1_out, or_2_out;
  wire [1:0] D0_q;

  or or_1 (or_1_out, D0_q[1], D0_q[0]);
  or or_2 (or_2_out, D0_q[1], D0_nq);
  D_FF_AS D1 (.Set(1'b0), .D(or_1_out), .C(CLK), .Clr(in_2), .Q(D0_q[1]));  // open: nQ
  D_FF_AS D0 (.Set(in_2), .D(or_2_out), .C(CLK), .Clr(1'b0), .Q(D0_q[0]), .nQ(D0_nq));
  Seven_Seg_Hex seven_seg_hex_1 (.d({{2{in_2}}, D0_q}), .dp(in_2));
endmodule
